# Fritzing sketch project1 (saved by Fritzing 0.9.2b)
circuit board: 8.46667cm x 5.64444cm
breadboards: 1

parts:
  Componente1 = Arduino Uno (Rev3) - ICSP
  R1 = Resistor [tolerance=±5% resistance=150 package="2512 [SMD]"]
  LED1 = LED - 5mm [color="Red (633nm)" package="5 mm [THT]"]

nets:
  N1: Componente1.D13/SCK, R1.Pin_1
  N2: Componente1.GND, LED1.cathode
  N3: R1.Pin_0, LED1.anode

// code stored in the sketch: project1.ino
//Programa : Pisca Led Arduino
//Autor : FILIPEFLOP

//Criando contador
int contador = 1000;
void setup()
{
//Define a porta do led como saida 
pinMode(13, OUTPUT);

Serial.begin(9600);
}

void loop()
{
//Acende o led 
digitalWrite(13, HIGH);

//Aguarda o intervalo especificado 
delay(contador);

//Apaga o led 
digitalWrite(13, LOW); 

//Aguarda o intervalo especificado 
delay(contador);
contador = contador*0.95;
Serial.print(contador, DEC);
Serial.print(", ");

if (contador == 0)
{
Serial.println("Reiniciando contador...");
contador = 1000;
Serial.print(contador, DEC);
Serial.print(", ");
}
}
