# Fritzing sketch project2 (saved by Fritzing 0.9.2b)
circuit board: 8.46667cm x 5.64444cm
breadboards: 1

parts:
  Componente1 = Arduino Uno (Rev3) - ICSP
  R1 = Resistor [tolerance=±5% resistance=1k package=THT]
  R2 = Resistor [tolerance=±5% resistance=220 package=THT]
  S1 = Pushbutton [package="[THT]"]
  U1 = 7-SEGMENT-DISPLAY [package=7-segment-display]

nets:
  N1: Componente1.5V, R1.Pin_1
  N2: Componente1.GND, R2.Pin_1, S1.Pin_3, S1.Pin_4
  N3: Componente1.D8, U1.E
  N4: Componente1.D9_PWM, U1.B
  N5: Componente1.D10_PWM/SS, R1.Pin_0, S1.Pin_1, S1.Pin_2
  N6: Componente1.D2, U1.G2
  N7: Componente1.D3_PWM, U1.A
  N8: Componente1.D4, U1.DP
  N9: Componente1.D5_PWM, U1.G1
  N10: Componente1.D6_PWM, U1.D
  N11: Componente1.D7, U1.G
  N12: R2.Pin_0, U1.F

// code stored in the sketch: project2.ino
int conta; //
 
byte displaySeteSeg[10][7] = { 
  
 { 1,1,1,1,1,1,0 },  //DIGITO 0
 { 0,1,1,0,0,0,0 },  //DIGITO 1
 { 1,1,0,1,1,0,1 },  //DIGITO 2
 { 1,1,1,1,0,0,1 },  //DIGITO 3
 { 0,1,1,0,0,1,1 },  //DIGITO 4
 { 1,0,1,1,0,1,1 },  //DIGITO 5
 { 1,0,1,1,1,1,1 },  //DIGITO 6
 { 1,1,1,0,0,0,0 },  //DIGITO 7
 { 1,1,1,1,1,1,1 },  //DIGITO 8
 { 1,1,1,1,0,1,1 }   //DIGITO 9
 
};
  
void setup(){
 
  //Definindo pinos como saída
  pinMode(2, OUTPUT);
  pinMode(3, OUTPUT);
  pinMode(4, OUTPUT);
  pinMode(5, OUTPUT);
  pinMode(6, OUTPUT);
  pinMode(7, OUTPUT);
  pinMode(8, OUTPUT);
  pinMode(9, OUTPUT);
  pinMode(10,INPUT);
 
  //inicializa display com número 0
  conta = 0;
  ligaSegmentosDisplay(conta);
    
}
 
void loop() {
 
  if(digitalRead(10)== LOW){ //Se o botão for pressionado soma +1 no display
     
    delay(500);
 
    conta++; //incremento
 
    if(conta == 10){ //Se passar de 9 reseta o display para 0
      conta = 0; 
      ligaSegmentosDisplay(conta);
    }
    else{ //Se não mostra no display o próximo número
      ligaSegmentosDisplay(conta);
    }
       
  }
   
}
 
void ligaSegmentosDisplay(byte digito){ //função para acionar o display com o digito correspondente
   
  byte pino = 2;
   
  //Liga os segmentos de acordo com o digito correspondente
  for (byte contadorSegmentos = 0; contadorSegmentos < 7; ++contadorSegmentos){ 
    digitalWrite(pino, displaySeteSeg[digito][contadorSegmentos]);
    ++pino; 
  }
}
